# Fritzing sketch station (saved by Fritzing 0.9.6b)
breadboards: 1

parts:
  WeMos_D1_Mini1 = WeMos D1 Mini
  C2 = Capacitor Polarized [package=panasonic_g]
  C3 = Capacitor [package=cap-pth-small2]
  U2 = LIPO-2000mAh [package=lipo-2000]
  U1 = Voltage Regulator [package=to-92]

nets:
  N1: WeMos_D1_Mini1.3V3, C2.+, C3.2, U1.OUT
  N2: WeMos_D1_Mini1.G, C2.-, C3.1, U2.-, U1.GND
  N3: U2.+, U1.IN
