# Fritzing sketch lol (saved by Fritzing 1.0.1rc)
breadboards: 1

parts:
  A1 = Esp32-c3 super mini
  S1 = 0.91 inch OLED I2C Display 128 x 32 Pixels
  VCC1 = Battery

nets:
  N1: A1.Pin_9, S1.GND
  N2: A1.Pin_10, S1.VCC
  N3: A1.Pin_11, S1.SCL
  N4: A1.Pin_12, S1.SDA
  N5: A1.Pin_14, VCC1.+
  N6: A1.Pin_15, VCC1.-

custom parts:
  Esp32-c3 super mini: ESP32-C3 Development Board ESP32 SuperMini Development Board ESP32 Development Board WiFi Bluetooth.
